# Fritzing sketch Board (saved by Fritzing 0.9.3b)
circuit board: 7.0889cm x 4.60441cm
breadboards: 1

parts:
  J1 = male pin header, 1 pin [form="♂ (male)"]
  J2 = male pin header, 1 pin [form="♂ (male)"]
  J3 = male pin header, 1 pin [form="♂ (male)"]
  J4 = male pin header, 1 pin [form="♂ (male)"]
  J5 = male pin header, 1 pin [form="♂ (male)"]
  J6 = male pin header, 1 pin [form="♂ (male)"]
  J7 = male pin header, 1 pin [form="♂ (male)"]
  J8 = male pin header, 1 pin [form="♂ (male)"]
  C1 = Electrolytic Capacitor [capacitance=47µF voltage=20V package="100 mil [THT, electrolytic]"]
  C2 = Ceramic Capacitor [capacitance=100nF package="100 mil [THT, multilayer]"]
  C3 = Ceramic Capacitor [capacitance=100nF package="100 mil [THT, multilayer]"]
  C4 = Electrolytic Capacitor [capacitance=47µF voltage=20V package="100 mil [THT, electrolytic]"]
  IC1 = IC, DIP package, 28 pins [chip_label=IC]
  C5 = Ceramic Capacitor [capacitance=10pF package="100 mil [THT, multilayer]"]
  XTAL1 = Crystal [frequency="16 MHz" package=THT]
  C6 = Ceramic Capacitor [capacitance=10pF package="100 mil [THT, multilayer]"]
  C8 = Ceramic Capacitor [capacitance=100nF package="100 mil [THT, multilayer]"]
  X1 = USB Connectors [package=usb-a-s-nosilk-female]
  R6 = Resistor [tolerance=±5% resistance=220 package=THT]
  C9 = Electrolytic Capacitor [capacitance=10µF package="100 mil [THT, electrolytic]"]
  C10 = Ceramic Capacitor [capacitance=1µF package="200 mil [THT, multilayer]"]
  R7 = Resistor [tolerance=±5% resistance=220 package=THT]
  R8 = Resistor [tolerance=±5% resistance=220 package=THT]
  LED1 = LED - 3mm [color="Red (633nm)" package="3 mm [THT]"]
  LED2 = LED - 3mm [color="Red (633nm)" package="3 mm [THT]"]
  LED3 = LED - 3mm [color="Red (633nm)" package="3 mm [THT]"]
  J10 = female pin header, 6 pins [form="♀ (female)"]
  R1 = Resistor [tolerance=±5% resistance=10k package=THT]
  R3 = Resistor [tolerance=±5% resistance=10k package=THT]
  R2 = Resistor [tolerance=±5% resistance=10k package=THT]
  J9 = female pin header, 2 pins [form="♀ (female)"]
  R4 = Resistor [tolerance=±5% resistance=10k package=THT]
  S1 = Momentary Switch [package=ksa_sealed_tac_switch]
  R9 = Resistor [tolerance=±5% resistance=1k package=THT]
  C11 = Electrolytic Capacitor [capacitance=0.1mF package="100 mil [THT, electrolytic]"]
  R10 = Resistor [tolerance=±5% resistance=10k package=THT]
  C12 = Ceramic Capacitor [capacitance=100nF package="100 mil [THT, multilayer]"]
  U1 = Voltage Regulator - 3.3V [package="TO220 [THT]"]
  C7 = Ceramic Capacitor [capacitance=1µF package="100 mil [THT, multilayer]"]

nets:
  N1: J1.pin1, C1.+, C2.0, IC1.pin15, X1.VBUS, C11.+, U1.GND
  N2: J2.pin1, IC1.pin11, IC1.pin14, R1.Pin_1
  N3: J3.pin1, IC1.pin16
  N4: J4.pin1, IC1.pin3, R3.Pin_1
  N5: J5.pin1, IC1.pin2, R2.Pin_0
  N6: J6.pin1, IC1.pin12, R4.Pin_0
  N7: J7.pin1, IC1.pin17
  3.3V/GND: J8.pin1, C1.-, C2.1, C3.1, C4.-, IC1.pin8, IC1.pin19, IC1.pin27, C5.0, C6.0, C8.1, X1.GND, C9.-, C10.1, J10.pin3, R1.Pin_0, R3.Pin_0, R2.Pin_1, R4.Pin_1, S1.1, S1.2, C11.-, C12.0, U1.output_voltage, C7.0
  5V: C3.0, C4.+, IC1.pin13, IC1.pin28, C8.0, C10.0, LED1.cathode, LED2.cathode, LED3.cathode, J10.pin2, R10.Pin_0, U1.input_voltage, C7.1
  /MCLR: IC1.pin1, J10.pin1, R9.Pin_1
  N8: IC1.pin4, J10.pin4
  N9: IC1.pin5, J10.pin5
  N10: IC1.pin6, J9.pin1
  N11: IC1.pin7, J9.pin2
  N12: IC1.pin9, XTAL1.pin_0, C6.1
  N13: IC1.pin10, C5.1, XTAL1.pin_1
  N14: IC1.pin18, R6.Pin_0
  N15: IC1.pin20, C9.+
  N16: IC1.pin21, X1.D+
  N17: IC1.pin22, X1.D-
  N18: IC1.pin24, R7.Pin_0
  N19: IC1.pin26, R8.Pin_0
  N20: R6.Pin_1, LED1.anode
  N21: R7.Pin_1, LED2.anode
  N22: R8.Pin_1, LED3.anode
  N23: S1.3, S1.4, R9.Pin_0, R10.Pin_1, C12.1
